// Logisim project CircuitoSimples.circ as structural Verilog: 2 circuits, main circuit main
module main (
);

  wire and_2_out, nand_1_out, undriven, undriven_2, undriven_3, undriven_4;

  nand nand_1 (nand_1_out, undriven, undriven_2);
  // AND_Gate and_1 has open pins: in0=undriven, in1=undriven_2, out=open
  and and_2 (and_2_out, undriven_3, undriven_4);
  // OR_Gate or_1 has open pins: in0=and_2_out, in1=nand_1_out, out=open

  // Notes on the sheet:
  //   A
  //   B
  //   C
  //   D
  //   C'D'
  //   AB
  //   AB +C'D'
endmodule

module AulaPraticasComLogisim (
  input  A,
  input  B,
  input  C,
  input  D,
  output A_B___C_D
);

  wire and_1_out, or_1_out, or_2_out;

  or or_1 (or_1_out, A, B);
  or or_2 (or_2_out, C, D);
  and and_1 (and_1_out, or_1_out, or_2_out);
  // Probe on nothing
endmodule
